// Digital circuit main.dig as structural Verilog
module main (
  input  [15:0] Bus,
  input  OE,
  input  Load,
  input  Crement,
  input  RCIi,
  input  Reset,
  input  CLK,
  input  RHLIn,
  input  Manual
);

  wire Register_Controller_p5, Register_Controller_p7, Register_Controller_p8, Register_Controller_p9,
       Register_Controller_p10, Register_Controller_p11, Register_Controller_p12, Register_Controller_p13,
       undriven_2, undriven_3, undriven_4, undriven_5;
  wire [3:2] undriven;
  wire [15:0] driver_1_out, registermodule_1_lho, registermodule_1_rho;

  LED led_1 (.in(driver_1_out[15]));
  LED led_2 (.in(driver_1_out[11]));
  LED led_3 (.in(driver_1_out[12]));
  LED led_4 (.in(driver_1_out[13]));
  LED led_5 (.in(driver_1_out[14]));
  LED led_6 (.in(driver_1_out[7]));
  LED led_7 (.in(driver_1_out[8]));
  LED led_8 (.in(driver_1_out[9]));
  LED led_9 (.in(driver_1_out[10]));
  LED led_10 (.in(driver_1_out[3]));
  LED led_11 (.in(driver_1_out[4]));
  LED led_12 (.in(driver_1_out[5]));
  LED led_13 (.in(driver_1_out[6]));
  LED led_14 (.in(driver_1_out[0]));
  LED led_15 (.in(driver_1_out[1]));
  LED led_16 (.in(driver_1_out[2]));
  assign driver_1_out = Manual ? Bus : 16'bz;  // Driver driver_1
  LED led_17 (.in(registermodule_1_lho[15]));
  LED led_18 (.in(registermodule_1_rho[15]));
  LED led_19 (.in(registermodule_1_lho[11]));
  LED led_20 (.in(registermodule_1_lho[12]));
  LED led_21 (.in(registermodule_1_lho[13]));
  LED led_22 (.in(registermodule_1_lho[14]));
  LED led_23 (.in(registermodule_1_rho[11]));
  LED led_24 (.in(registermodule_1_rho[12]));
  LED led_25 (.in(registermodule_1_rho[13]));
  LED led_26 (.in(registermodule_1_rho[14]));
  LED led_27 (.in(registermodule_1_lho[7]));
  LED led_28 (.in(registermodule_1_lho[8]));
  LED led_29 (.in(registermodule_1_lho[9]));
  LED led_30 (.in(registermodule_1_lho[10]));
  LED led_31 (.in(registermodule_1_rho[7]));
  LED led_32 (.in(registermodule_1_rho[8]));
  LED led_33 (.in(registermodule_1_rho[9]));
  LED led_34 (.in(registermodule_1_rho[10]));
  LED led_35 (.in(registermodule_1_lho[3]));
  LED led_36 (.in(registermodule_1_lho[4]));
  LED led_37 (.in(registermodule_1_lho[5]));
  LED led_38 (.in(registermodule_1_lho[6]));
  LED led_39 (.in(registermodule_1_rho[3]));
  LED led_40 (.in(registermodule_1_rho[4]));
  LED led_41 (.in(registermodule_1_rho[5]));
  LED led_42 (.in(registermodule_1_rho[6]));
  RegisterModule registermodule_1 (
    .OE(OE), .LHOEi(Register_Controller_p13), .OUT(driver_1_out), .RHOEi(undriven_5),
    .LHO(registermodule_1_lho), .RHO(registermodule_1_rho), .IN(driver_1_out), .CLK(CLK), .INC(undriven[2]),
    .DEC(undriven[3]), .Reset(Reset), .Load(Load), .Enablei(Register_Controller_p9),
    .RHBusIn(registermodule_1_rho), .RHIN(RHLIn));
  RegisterModule registermodule_2 (
    .OE(OE), .LHOEi(Register_Controller_p12), .OUT(driver_1_out), .RHOEi(undriven_4),
    .LHO(registermodule_1_lho), .RHO(registermodule_1_rho), .IN(driver_1_out), .CLK(CLK), .INC(undriven[2]),
    .DEC(undriven[3]), .Reset(Reset), .Load(Load), .Enablei(Register_Controller_p8),
    .RHBusIn(registermodule_1_rho), .RHIN(RHLIn));
  RegisterModule registermodule_3 (
    .OE(OE), .LHOEi(Register_Controller_p11), .OUT(driver_1_out), .RHOEi(undriven_3),
    .LHO(registermodule_1_lho), .RHO(registermodule_1_rho), .IN(driver_1_out), .CLK(CLK), .INC(undriven[2]),
    .DEC(undriven[3]), .Reset(Reset), .Load(Load), .Enablei(Register_Controller_p7),
    .RHBusIn(registermodule_1_rho), .RHIN(RHLIn));
  RegisterModule registermodule_4 (
    .OE(OE), .LHOEi(Register_Controller_p10), .OUT(driver_1_out), .RHOEi(undriven_2),
    .LHO(registermodule_1_lho), .RHO(registermodule_1_rho), .IN(driver_1_out), .CLK(CLK), .INC(undriven[2]),
    .DEC(undriven[3]), .Reset(Reset), .Load(Load), .Enablei(Register_Controller_p5),
    .RHBusIn(registermodule_1_rho), .RHIN(RHLIn));
  LED led_43 (.in(registermodule_1_lho[0]));
  LED led_44 (.in(registermodule_1_lho[1]));
  LED led_45 (.in(registermodule_1_lho[2]));
  LED led_46 (.in(registermodule_1_rho[0]));
  LED led_47 (.in(registermodule_1_rho[1]));
  LED led_48 (.in(registermodule_1_rho[2]));
  // RegisterController Register_Controller: pin names not known; wires that end beside it: driver_1_out, CLK, Reset, Crement, Register_Controller_p5, RCIi, Register_Controller_p7, Register_Controller_p8, Register_Controller_p9, Register_Controller_p10, Register_Controller_p11, Register_Controller_p12, Register_Controller_p13

  // Notes on the sheet:
  //   RCIi: default 1
  //   RHLIn: If active, enabled register will load
  //   from the right hand bus instead of the
  //   main bus. This is used to move data
  //   from register to register
  //   Manual: Manually put data on bus
  //   Main Bus
  //   Left Hand Bus
  //   Right Hand Bus
  //   Register Control Bus
endmodule
